// Logisim project cpu.circ as structural Verilog: 7 circuits, main circuit main
// CPU
module main (
  input  [31:0] RS_READ_VALUE,
  input  [31:0] RI_READ_VALUE,
  input  [31:0] RD_READ_VALUE,
  input  [31:0] JC_READ_VALUE,
  input  [31:0] INSTRUCTION,
  input  CLOCK,
  output [4:0] RS,
  output [4:0] RI,
  output [4:0] RD,
  output [31:0] RD_WRITE_VALUE,
  output RD_WRITE_ENABLE,
  output [23:0] FETCH_ADDRESS
);

  wire jump_control, jump_imm, mem_to_reg, MW, pc_store, u_control_1_alu_src, u_decode_1_i, WM;
  wire [2:0] u_decode_1_jc;
  wire [3:0] u_control_1_alu_control, u_decode_1_op;
  wire [4:0] _RD_t;
  wire [16:0] Imm;
  wire [23:0] adder_1_out, Addr, bit_extender_1_out, multiplexer_1_out, multiplexer_2_out;
  wire [24:0] bit_extender_4_out;
  wire [31:0] bit_extender_3_out, multiplexer_3_out, multiplexer_4_out, pc_1, u_alu_1_alu_result,
       u_mem_1_data_out;

  Register #(.width(24)) register_1 (.D(multiplexer_2_out), .Q(FETCH_ADDRESS), .clk(CLOCK));  // open: en, clr
  u_decode u_decode_1 (
    .in_1(INSTRUCTION), .OP(u_decode_1_op), .JC(u_decode_1_jc), .I(u_decode_1_i), .RD(_RD_t), .RS(RS),
    .RI(RI), .Immediate(Imm), .Addr(Addr), .pc_1_store_control(pc_store));
  u_control u_control_1 (
    .OP(u_decode_1_op), .JC(u_decode_1_jc), .I(u_decode_1_i), .JC_2(JC_READ_VALUE),
    .ALU_Control(u_control_1_alu_control), .ALU_Src(u_control_1_alu_src), .RD_Write_Enable(RD_WRITE_ENABLE),
    .J_Src(jump_imm), .Mem_to_Reg(mem_to_reg), .PC_control(jump_control), .WORD_MODE(WM), .MEM_WRITE(MW));  // open: JC_control
  Adder #(.width(24)) adder_1 (.a(FETCH_ADDRESS), .b(24'h1), .out(adder_1_out));  // open: cin, cout
  Multiplexer #(.width(24), .enable("false")) multiplexer_1 (
    .in0(bit_extender_1_out), .in1(Addr), .out(multiplexer_1_out), .sel(jump_imm));
  Bit_Extender #(.in_width(32), .out_width(24)) bit_extender_1 (.in(RI_READ_VALUE), .out(bit_extender_1_out));
  assign pc_1 = {{8{1'b0}}, adder_1_out};  // Bit_Extender bit_extender_2
  Multiplexer #(.width(24), .enable("false")) multiplexer_2 (
    .in0(adder_1_out), .in1(multiplexer_1_out), .out(multiplexer_2_out), .sel(jump_control));
  assign bit_extender_3_out = {{15{Imm[16]}}, Imm};  // Bit_Extender bit_extender_3
  Multiplexer #(.width(32), .enable("false")) multiplexer_3 (
    .in0(RI_READ_VALUE), .in1(bit_extender_3_out), .out(multiplexer_3_out), .sel(u_control_1_alu_src));
  u_MEM u_mem_1 (
    .ADDRESS(bit_extender_4_out), .DATA_OUT(u_mem_1_data_out), .WORD_MODE(WM), .MEM_WRITE(MW),
    .DATA_IN(RD_READ_VALUE), .CLOCK(CLOCK));
  u_ALU u_alu_1 (
    .ALU_RESULT(u_alu_1_alu_result), .ALU_CONTROL(u_control_1_alu_control), .ALU_Y(multiplexer_3_out));  // open: ALU_X
  Bit_Extender #(.in_width(32), .out_width(25)) bit_extender_4 (.in(u_alu_1_alu_result), .out(bit_extender_4_out));
  Multiplexer #(.width(32), .enable("false")) multiplexer_4 (
    .in0(u_alu_1_alu_result), .in1(u_mem_1_data_out), .out(multiplexer_4_out), .sel(mem_to_reg));
  Multiplexer #(.width(32), .enable("false")) multiplexer_5 (
    .in0(multiplexer_4_out), .in1(pc_1), .out(RD_WRITE_VALUE), .sel(pc_store));

  // Other names for the same wires on the sheet: _RD[4:0] = RD; _RI[4:0] = RI; _RS[4:0] = RS; CLK = CLOCK;
  //   FA[23:0] = FETCH_ADDRESS; INST[31:0] = INSTRUCTION; JC_READ[31:0] = JC_READ_VALUE;
  //   RD_READ[31:0] = RD_READ_VALUE; RDWE = RD_WRITE_ENABLE; RDWV[31:0] = RD_WRITE_VALUE;
  //   RI_READ[31:0] = RI_READ_VALUE; RS_READ[31:0] = RS_READ_VALUE
endmodule

module u_ALU (
  input  [3:0] ALU_CONTROL,
  input  [31:0] ALU_X,
  input  [31:0] ALU_Y,
  output [31:0] ALU_RESULT
);

  wire and_2_out, bit_extender_5_out, comparator_1_eq, comparator_2_gt;
  wire [4:0] bit_extender_1_out, bit_extender_2_out, bit_extender_3_out;
  wire [31:0] _00_SL, _01_SR, _02_And, _03_OR, _04_REV, _05_XOR, _06_ADD, _07_SUB, _08_MUL, _09_DIV,
       bit_extender_4_out, multiplexer_1_out, shifter_2_out, shifter_3_out, subtractor_2_out;

  Bit_Extender #(.in_width(32), .out_width(5)) bit_extender_1 (.in(ALU_Y), .out(bit_extender_1_out));
  Bit_Extender #(.in_width(32), .out_width(5)) bit_extender_2 (.in(ALU_Y), .out(bit_extender_2_out));
  assign _02_And = ALU_X & ALU_Y;  // AND_Gate and_1, 32 bits wide
  assign _03_OR = ALU_X | ALU_Y;  // OR_Gate or_1, 32 bits wide
  Bit_Extender #(.in_width(32), .out_width(5)) bit_extender_3 (.in(ALU_Y), .out(bit_extender_3_out));
  assign _05_XOR = ALU_X ^ ALU_Y;  // XOR_Gate xor_1, 32 bits wide
  Adder #(.width(32)) adder_1 (.a(ALU_X), .b(ALU_Y), .out(_06_ADD));  // open: cin, cout
  Subtractor #(.width(32)) subtractor_1 (.a(ALU_X), .b(ALU_Y), .out(_07_SUB));  // open: bin, bout
  Multiplier #(.width(32)) multiplier_1 (.a(ALU_X), .b(ALU_Y), .out(_08_MUL));  // open: cin, cout
  Divider #(.width(32)) divider_1 (.a(ALU_X), .b(ALU_Y), .out(_09_DIV));  // open: upper, rem
  assign bit_extender_4_out = {{31{1'b0}}, bit_extender_5_out};  // Bit_Extender bit_extender_4
  Bit_Extender #(.in_width(32), .out_width(1)) bit_extender_5 (.in(ALU_X), .out(bit_extender_5_out));
  Shifter #(.width(32), .shift("ar")) shifter_1 (.in(ALU_X), .\dist (bit_extender_2_out), .out(_01_SR));
  u_REV u_rev_1 (.REVERSE_AMOUNT(bit_extender_3_out), .OUTPUT(_04_REV), .INPUT(ALU_X));
  Shifter #(.width(32)) shifter_2 (.in(bit_extender_4_out), .\dist (bit_extender_1_out), .out(shifter_2_out));
  Subtractor #(.width(32)) subtractor_2 (.a(shifter_2_out), .b(32'h1), .out(subtractor_2_out));  // open: bin, bout
  Divider divider_2 ();  // open: a, b, out, upper, rem
  Comparator #(.width(32)) comparator_1 (.a(bit_extender_4_out), .b(32'h1), .eq(comparator_1_eq));  // open: gt, lt
  Comparator #(.width(32)) comparator_2 (.a(ALU_Y), .b({32{1'b0}}), .gt(comparator_2_gt));  // open: eq, lt
  Shifter #(.width(32)) shifter_3 (.in(ALU_X), .\dist (bit_extender_1_out), .out(shifter_3_out));
  Multiplexer #(.width(32), .enable("false")) multiplexer_1 (
    .in0({32{1'b0}}), .in1(subtractor_2_out), .out(multiplexer_1_out), .sel(and_2_out));
  and and_2 (and_2_out, comparator_1_eq, comparator_2_gt);
  Adder #(.width(32)) adder_2 (.a(shifter_3_out), .b(multiplexer_1_out), .out(_00_SL));  // open: cin, cout
  Multiplexer #(.select(4), .width(32), .enable("false")) multiplexer_2 (
    .in0(_00_SL), .in1(_01_SR), .in2(_02_And), .in3(_03_OR), .in4(_04_REV), .in5(_05_XOR), .in6(_06_ADD),
    .in7(_07_SUB), .in8(_08_MUL), .in9(_09_DIV), .in10(_06_ADD), .in11(_06_ADD), .in12(_06_ADD),
    .in13(_06_ADD), .in14({ALU_Y[16:0], ALU_X[14:0]}), .out(ALU_RESULT), .sel(ALU_CONTROL));  // open: in15

  // Other names for the same wires on the sheet: _14_STU[31:0] = {ALU_Y[16:0], ALU_X[14:0]}; X[31:0] = ALU_X;
  //   Y[31:0] = ALU_Y
endmodule

// Data Memory
module u_MEM (
  input  [24:0] ADDRESS,
  input  WORD_MODE,
  input  MEM_WRITE,
  input  [31:0] DATA_IN,
  input  CLOCK,
  output [31:0] DATA_OUT
);

  wire and_1_out, and_2_out, not_1_out, not_2_out, not_3_out;
  wire [15:0] DATA_EVEN, DATA_ODD, multiplexer_4_out, multiplexer_5_out, ram_1_data, ram_2_data;
  wire [23:0] adder_1_out, multiplexer_3_out;
  wire [31:0] adder_2_out, bit_extender_1_out, bit_extender_2_out, shifter_1_out;

  Multiplexer #(.width(16), .enable("false")) multiplexer_1 (
    .in0(DATA_IN[31:16]), .in1(DATA_IN[15:0]), .out(DATA_ODD), .sel(ADDRESS[0]));
  Multiplexer #(.width(16), .enable("false")) multiplexer_2 (
    .in0(DATA_IN[15:0]), .in1(DATA_IN[31:16]), .out(DATA_EVEN), .sel(ADDRESS[0]));
  Multiplexer #(.width(24), .enable("false")) multiplexer_3 (
    .in0(ADDRESS[24:1]), .in1(adder_1_out), .out(multiplexer_3_out), .sel(ADDRESS[0]));
  Adder #(.width(24)) adder_1 (.a(ADDRESS[24:1]), .b(24'h1), .out(adder_1_out));  // open: cin, cout
  not not_1 (not_1_out, and_1_out);
  not not_2 (not_2_out, and_2_out);
  RAM #(.addrWidth(24), .dataWidth(16), .bus("separate")) ram_1 (
    .addr(multiplexer_3_out), .din(DATA_EVEN), .data(ram_1_data), .str(and_1_out), .clk(CLOCK), .ld(not_1_out));  // open: sel, clr
  and and_1 (and_1_out, ADDRESS[0], MEM_WRITE);
  RAM #(.addrWidth(24), .dataWidth(16), .bus("separate")) ram_2 (
    .addr(ADDRESS[24:1]), .din(DATA_ODD), .data(ram_2_data), .str(and_2_out), .clk(CLOCK), .ld(not_2_out));  // open: sel, clr
  not not_3 (not_3_out, ADDRESS[0]);
  and and_2 (and_2_out, not_3_out, MEM_WRITE);
  assign bit_extender_1_out = {{16{1'b0}}, multiplexer_4_out};  // Bit_Extender bit_extender_1
  Multiplexer #(.width(16), .enable("false")) multiplexer_4 (
    .in0(ram_1_data), .in1(ram_2_data), .out(multiplexer_4_out), .sel(ADDRESS[0]));
  Multiplexer #(.width(16), .enable("false")) multiplexer_5 (
    .in0(ram_2_data), .in1(ram_1_data), .out(multiplexer_5_out), .sel(ADDRESS[0]));
  assign bit_extender_2_out = {{16{1'b0}}, multiplexer_5_out};  // Bit_Extender bit_extender_2
  Shifter #(.width(32)) shifter_1 (.in(bit_extender_2_out), .\dist (5'b10000), .out(shifter_1_out));
  Multiplexer #(.width(32), .enable("false")) multiplexer_6 (
    .in0(bit_extender_1_out), .in1(adder_2_out), .out(DATA_OUT), .sel(WORD_MODE));
  Adder #(.width(32)) adder_2 (.a(bit_extender_1_out), .b(shifter_1_out), .out(adder_2_out));  // open: cin, cout

  // Other names for the same wires on the sheet: ADDR[24:0] = ADDRESS; CLK = CLOCK; MEM = MEM_WRITE;
  //   W_MODE = WORD_MODE

  // Notes on the sheet:
  //   Even
  //   Odd
  //   You might use the word mode input to differentiate LW/SW from LH/SH.
  //   However, you *SHOULD* use 2 RAM modules, one for even addresses and one for odd addresses.
endmodule

module u_REV (
  input  [4:0] REVERSE_AMOUNT,
  input  [31:0] INPUT,
  output [31:0] OUTPUT
);

  wire [31:0] multiplexer_1_out, multiplexer_2_out, multiplexer_3_out, multiplexer_4_out;

  Multiplexer #(.width(32), .enable("false")) multiplexer_1 (
    .in0(INPUT),
    .in1({INPUT[30], INPUT[31], INPUT[28], INPUT[29], INPUT[26], INPUT[27], INPUT[24], INPUT[25], INPUT[22], INPUT[23], INPUT[20], INPUT[21], INPUT[18], INPUT[19], INPUT[16], INPUT[17], INPUT[14], INPUT[15], INPUT[12], INPUT[13], INPUT[10], INPUT[11], INPUT[8], INPUT[9], INPUT[6], INPUT[7], INPUT[4], INPUT[5], INPUT[2], INPUT[3], INPUT[0], INPUT[1]}),
    .out(multiplexer_1_out), .sel(REVERSE_AMOUNT[0]));
  Multiplexer #(.width(32), .enable("false")) multiplexer_2 (
    .in0(multiplexer_1_out),
    .in1({multiplexer_1_out[29:28], multiplexer_1_out[31:30], multiplexer_1_out[25:24], multiplexer_1_out[27:26], multiplexer_1_out[21:20], multiplexer_1_out[23:22], multiplexer_1_out[17:16], multiplexer_1_out[19:18], multiplexer_1_out[13:12], multiplexer_1_out[15:14], multiplexer_1_out[9:8], multiplexer_1_out[11:10], multiplexer_1_out[5:4], multiplexer_1_out[7:6], multiplexer_1_out[1:0], multiplexer_1_out[3:2]}),
    .out(multiplexer_2_out), .sel(REVERSE_AMOUNT[1]));
  Multiplexer #(.width(32), .enable("false")) multiplexer_3 (
    .in0(multiplexer_2_out),
    .in1({multiplexer_2_out[26], multiplexer_2_out[27], multiplexer_2_out[24], multiplexer_2_out[25], multiplexer_2_out[30], multiplexer_2_out[31], multiplexer_2_out[28], multiplexer_2_out[29], multiplexer_2_out[18], multiplexer_2_out[19], multiplexer_2_out[16], multiplexer_2_out[17], multiplexer_2_out[22], multiplexer_2_out[23], multiplexer_2_out[20], multiplexer_2_out[21], multiplexer_2_out[10], multiplexer_2_out[11], multiplexer_2_out[8], multiplexer_2_out[9], multiplexer_2_out[14], multiplexer_2_out[15], multiplexer_2_out[12], multiplexer_2_out[13], multiplexer_2_out[2], multiplexer_2_out[3], multiplexer_2_out[0], multiplexer_2_out[1], multiplexer_2_out[6], multiplexer_2_out[7], multiplexer_2_out[4], multiplexer_2_out[5]}),
    .out(multiplexer_3_out), .sel(REVERSE_AMOUNT[2]));
  Multiplexer #(.width(32), .enable("false")) multiplexer_4 (
    .in0(multiplexer_3_out),
    .in1({multiplexer_3_out[23:16], multiplexer_3_out[31:24], multiplexer_3_out[7:0], multiplexer_3_out[15:8]}),
    .out(multiplexer_4_out), .sel(REVERSE_AMOUNT[3]));
  Multiplexer #(.width(32), .enable("false")) multiplexer_5 (
    .in0(multiplexer_4_out), .in1({multiplexer_4_out[15:0], multiplexer_4_out[31:16]}), .out(OUTPUT),
    .sel(REVERSE_AMOUNT[4]));

  // Other names for the same wires on the sheet: rev_0 = REVERSE_AMOUNT[0]; rev_1 = REVERSE_AMOUNT[1];
  //   rev_2 = REVERSE_AMOUNT[2]; rev_3 = REVERSE_AMOUNT[3]; rev_4 = REVERSE_AMOUNT[4]
endmodule

module u_decode (
  input  [31:0] in_1,
  output [3:0] OP,
  output [2:0] JC,
  output I,
  output [4:0] RD,
  output [4:0] RS,
  output [4:0] RI,
  output [16:0] Immediate,
  output [23:0] Addr,
  output pc_1_store_control
);

  wire comparator_1_eq, comparator_2_eq;

  Comparator #(.width(4), .mode("unsigned")) comparator_1 (
    .a(in_1[31:28]), .b(4'b1111), .eq(comparator_1_eq));  // open: gt, lt
  Comparator #(.width(3), .mode("unsigned")) comparator_2 (
    .a(in_1[26:24]), .b(3'b111), .eq(comparator_2_eq));  // open: gt, lt
  Multiplexer #(.width(5), .enable("false")) multiplexer_1 (
    .in0(in_1[26:22]), .in1(5'b00110), .out(RD), .sel(pc_1_store_control));
  and and_1 (pc_1_store_control, comparator_1_eq, comparator_2_eq);

  assign Addr = in_1[23:0];
  assign I = in_1[27];
  assign Immediate = in_1[16:0];
  assign JC = in_1[26:24];
  assign OP = in_1[31:28];
  assign RI = in_1[4:0];
  assign RS = in_1[21:17];

  // Other names for the same wires on the sheet: Inst[31:0] = in_1
endmodule

module u_control (
  input  [3:0] OP,
  input  [2:0] JC,
  input  I,
  input  [31:0] JC_2,
  output [3:0] ALU_Control,
  output [2:0] JC_control,
  output ALU_Src,
  output RD_Write_Enable,
  output J_Src,
  output Mem_to_Reg,
  output PC_control,
  output WORD_MODE,
  output MEM_WRITE
);

  wire and_2_out, comparator_2_eq, comparator_3_eq, comparator_4_eq, comparator_5_eq, comparator_6_eq,
       comparator_7_gt, comparator_8_lt, comparator_9_eq, not_1_out, or_2_out;

  u_jump_control u_jump_control_1 (.jc(JC_2), .OP(OP), .jc_2(JC), .pc_control(PC_control));
  Comparator #(.width(4), .mode("unsigned")) comparator_1 (.a(OP), .b(4'b1011), .gt(WORD_MODE));  // open: eq, lt
  Comparator #(.width(4), .mode("unsigned")) comparator_2 (.a(OP), .b(4'b1011), .eq(comparator_2_eq));  // open: gt, lt
  Comparator #(.width(4), .mode("unsigned")) comparator_3 (.a(OP), .b(4'b1101), .eq(comparator_3_eq));  // open: gt, lt
  or or_1 (MEM_WRITE, comparator_2_eq, comparator_3_eq);
  Comparator #(.width(4), .mode("unsigned")) comparator_4 (.a(OP), .b(4'b1011), .eq(comparator_4_eq));  // open: gt, lt
  Comparator #(.width(4), .mode("unsigned")) comparator_5 (.a(OP), .b(4'b1101), .eq(comparator_5_eq));  // open: gt, lt
  Comparator #(.width(4), .mode("unsigned")) comparator_6 (.a(OP), .b(4'b1111), .eq(comparator_6_eq));  // open: gt, lt
  Comparator #(.width(4), .mode("unsigned")) comparator_7 (.a(OP), .b(4'b1001), .gt(comparator_7_gt));  // open: eq, lt
  Comparator #(.width(4), .mode("unsigned")) comparator_8 (.a(OP), .b(4'b1110), .lt(comparator_8_lt));  // open: gt, eq
  Comparator #(.width(3), .mode("unsigned")) comparator_9 (.a(JC), .b(3'b111), .eq(comparator_9_eq));  // open: gt, lt
  and and_1 (Mem_to_Reg, comparator_7_gt, comparator_8_lt);
  and and_2 (and_2_out, comparator_6_eq, not_1_out);
  not not_1 (not_1_out, comparator_9_eq);
  not not_2 (RD_Write_Enable, or_2_out);
  or or_2 (or_2_out, comparator_4_eq, comparator_5_eq, and_2_out);

  assign ALU_Control = OP;
  assign ALU_Src = I;
  assign J_Src = I;
  assign JC_control = JC;
endmodule

module u_jump_control (
  input  [31:0] jc,
  input  [2:0] jc_2,
  input  [3:0] OP,
  output pc_control
);

  wire _1, _2, _3, _4, _5, _6, comparator_2_eq, multiplexer_1_out;

  Comparator #(.width(32)) comparator_1 (.a(jc), .b({32{1'b0}}), .gt(_1), .eq(_2), .lt(_3));
  not not_1 (_4, _1);
  not not_2 (_5, _2);
  not not_3 (_6, _3);
  Multiplexer #(.select(3), .enable("false")) multiplexer_1 (
    .in0(1'b1), .in1(_1), .in2(_2), .in3(_3), .in4(_4), .in5(_5), .in6(_6), .in7(1'b1),
    .out(multiplexer_1_out), .sel(jc_2));
  and and_1 (pc_control, multiplexer_1_out, comparator_2_eq);
  Comparator #(.width(4), .mode("unsigned")) comparator_2 (.a(OP), .b(4'b1111), .eq(comparator_2_eq));  // open: gt, lt

  // Other names for the same wires on the sheet: comp[31:0] = jc
endmodule
